# Fritzing sketch Fritzing (saved by Fritzing 0.9.3b)
breadboards: 1

parts:
  Composant1 = Arduino Uno (Rev3)
  R1 = Resistor [tolerance=±5% resistance=10 package=THT]
  L1 = Inductor [package="400 mil [THT]"]
  R2 = Resistor [tolerance=±5% resistance=3.3 package=THT]
  D1 = Rectifier Diode [part_number=1N4001 package="300 mil [THT]"]
  C1 = Ceramic Capacitor [capacitance=10nF package="100 mil [THT, multilayer]"]
  R3 = Resistor [tolerance=±5% resistance=220 package=THT]
  C2 = Ceramic Capacitor [capacitance=100nF package="100 mil [THT, multilayer]"]
  LED1 = LED - 5mm [color="Yellow (585nm)" package="5 mm [THT]"]
  LED2 = LED - 5mm [color="Red (633nm)" package="5 mm [THT]"]
  LED3 = LED - 5mm [color="Green (555nm)" package="5 mm [THT]"]

nets:
  N1: Composant1.A0, D1.cathode, R3.Pin_1, C2.1
  N2: Composant1.D9_PWM, R1.Pin_1
  N3: Composant1.GND, R2.Pin_0, R3.Pin_0, C2.0
  N4: Composant1.D2, LED3.anode
  N5: Composant1.D3_PWM, LED1.anode
  N6: Composant1.D4, LED2.anode
  N7: R1.Pin_0, L1.pin_1, R2.Pin_1
  N8: L1.pin_0, D1.anode, C1.0
  N9: LED1.cathode, LED2.cathode, LED3.cathode
